# Fritzing sketch Proiect_Racheta_Constanta (saved by Fritzing 1.0.4)
breadboards: 1

parts:
  Part1 = Arduino Uno (Rev3)
  Part2 = Thumb Joystick
  Part3 = Thumb Joystick
  Part4 = LCD1602-I2C
  HC-SR04_Sensor_1 = HC-SR04 Ultrasonic Distance Sensor
  J4 = Basic Servo
  J3 = Basic Servo
  J2 = Basic Servo
  J1 = Basic Servo

nets:
  N1: Part1.A0, Part2.HORZ
  N2: Part1.A1, Part2.VERT
  N3: Part1.A2, Part3.HORZ
  N4: Part1.A3, Part3.VERT
  N5: Part1.A4/SDA, Part4.SDA
  N6: Part1.A5/SCL, Part4.SCL
  N7: Part1.D8, J2.pulse
  N8: Part1.D9_PWM, J1.pulse
  N9: Part1.D10_PWM/SS, HC-SR04_Sensor_1.TRIG
  N10: Part1.D11_PWM/MOSI, HC-SR04_Sensor_1.ECHO
  N11: Part1.D2, Part2.SEL
  N12: Part1.D3_PWM, J4.pulse
  N13: Part1.D4, Part3.SEL
  N14: Part1.D5_PWM, J3.pulse
  VCC: Part1.5V, Part2.VCC, Part3.VCC, Part4.VCC, HC-SR04_Sensor_1.VCC, J4.vcc, J3.vcc, J2.vcc, J1.vcc
  GND: Part1.GND, Part2.GND, Part3.GND, Part4.GND, HC-SR04_Sensor_1.GND, J4.gnd, J3.gnd, J2.gnd, J1.gnd

custom parts:
  LCD1602-I2C: A standard character display, usually with 2x16 characters. Comes in many colors with LCM1602 IIC attached.
